// Digital circuit CPU.dig as structural Verilog
module CPU (
  input  S,
  input  S_2,
  input  S_3,
  input  S_4,
  input  [7:0] IN,
  input  [7:0] IN_2,
  input  in_7
);

  wire cpu_clk_1_p1, cpu_clk_1_p4, cpu_clk_1_p5, cpu_clk_1_p6, undriven, undriven_3, undriven_5, undriven_6,
       undriven_7;
  wire [7:0] cpu_clk_1_p2, undriven_2, undriven_4, undriven_8;

  cpu_temp cpu_temp_1 (
    .I({undriven_8[0], undriven_8[1], undriven_8[2], undriven_8[3], undriven_8[4], undriven_8[5], undriven_8[6], undriven_8[7]}),
    .S(undriven));  // open: O
  cpu_bus BUS1 (.Bus1(S), .\Ì (undriven_2));  // open: O
  cpu_alu ALU ();
  // cpu_clk cpu_clk_1: pin names not known; wires that end beside it: cpu_clk_1_p1, cpu_clk_1_p2, in_7, cpu_clk_1_p4, cpu_clk_1_p5, cpu_clk_1_p6
  cpu_reg_8 ACC (.I(cpu_clk_1_p2), .E(undriven_3));  // open: S, O
  cpu_reg_8 REG0 (.I(IN), .E(1'b1));  // open: S, O
  cpu_reg_8 REG1 (.I(IN_2), .E(1'b1));  // open: S, O
  Control control_1 ();
  cpu_reg_8 REG2 (.I(undriven_8), .E(undriven_5));  // open: S, O
  cpu_reg_8 REG3 (.I(undriven_8), .E(undriven_6));  // open: S, O
  cpu_ram_256 cpu_ram_256_1 (
    .Address({undriven_8[0], undriven_8[1], undriven_8[2], undriven_8[3], undriven_8[4], undriven_8[5], undriven_8[6], undriven_8[7]}),
    .Reset(undriven_7), .En(1'b0), .I(undriven_4));  // open: Set_adr, Set, O
endmodule
